// Digital circuit DigLo67_Project_Full-183100.dig as structural Verilog
module DigLo67_Project_Full_183100 (
  input  [7:0] M,
  input  [7:0] N,
  input  reset,
  input  progLoad,
  input  start,
  input  result,
  input  clk,
  input  [12:0] progIN,
  output valid,
  output [4:0] out_10,
  output [7:0] out_11,
  output [7:0] out_12,
  output [7:0] out_13,
  output [7:0] out_14,
  output [4:0] out_15,
  output [7:0] out_16,
  output done,
  output [7:0] \output ,
  output [7:0] out_19,
  output [7:0] out_20,
  output [7:0] out_21,
  output [7:0] out_22,
  output [7:0] out_23,
  output [7:0] out_24
);

  wire A0NEW, A1NEW, A2NEW, A3NEW, Ag, and_1_out, and_2_out, and_3_out, and_13_out, and_14_out, and_15_out,
       and_16_out, and_17_out, and_18_out, and_19_out, and_20_out, and_21_out, and_22_out, busy, busy2,
       clear, comparator_1_eq, comparator_3_gt, counter_3_out, d_ff_11_q, Eq, equal_flag, future, futurehold,
       greater_flag, Id, Id2, lesser_flag, Loada, Loadb, multiplexer_10_out, multiplexer_18_out,
       multiplexer_23_out, not_2_out, not_5_out, not_6_out, opcode11101, opcode11101hold, opcode11111,
       or_1_out, or_2_out, or_3_out, or_13_out, or_16_out, or_17_out, or_18_out, or_19_out, or_20_out,
       or_21_out, or_22_out, or_23_out, or_24_out, or_25_out, prime, Qa, Qb, ResetCounter2Jump,
       ResetCounter2Jumphold, resethold, resulthold, rRAMActive, starthold;
  wire [1:0] counter_4_out;
  wire [4:0] opcode2, pRAM_d1_2;
  wire [5:0] A_B2;
  wire [7:0] _1A, A_B, A_B_t, A_B_t_t, A_B_t_t_t, A_plus_B, a_t, add_2_s, add_3_s, addressrRAM, b_t, Bitand,
       Bitor, Bitxor, Counter, Counter2, counter_5_out, counter_6_out, counter_7_out, d_ff_1_q, d_ff_2_q,
       GCDOUTPUT, multiplexer_2_out, multiplexer_8_out, multiplexer_9_out, multiplexer_13_out,
       multiplexer_19_out, multiplexer_20_out, multiplexer_21_out, multiplexer_24_out, multiplexer_28_out,
       neg_1_out, Oprandjump, pRAM_d1, pRAMtoacc, rRAMtoaccNew, SelaccA, SelaccB, SelregC, shift, sub_2_s,
       sub_3_s, sub_4_s;
  wire [11:0] _3A, _4A, _5A, _6A, _7A, A_A;
  wire [15:0] mul_8_mul;

  Multiplexer #(.Selector_Bits(5)) multiplexer_1 (
    .sel(out_10), .in_0(1'b0), .in_1(1'b0), .in_2(1'b0), .in_3(1'b0), .in_4(1'b0), .in_5(1'b0), .in_6(1'b0),
    .in_7(1'b0), .in_8(1'b0), .in_9(1'b0), .in_10(1'b0), .in_11(1'b0), .in_12(1'b0), .in_13(1'b0),
    .in_14(1'b0), .in_15(1'b0), .in_16(1'b0), .in_17(1'b0), .in_18(1'b0), .in_19(1'b0), .in_20(1'b0),
    .in_21(1'b0), .in_22(1'b0), .in_23(1'b0), .in_24(1'b0), .in_25(1'b0), .in_26(1'b0), .in_27(1'b0),
    .in_28(1'b0), .in_29(1'b1), .in_30(1'b0), .in_31(1'b0), .out(opcode11101));
  Mul #(.Bits(6)) mul_1 (.a(out_12[5:0]), .b(out_12[5:0]), .mul(A_A));
  Mul #(.Bits(6)) mul_2 (.a(A_A[5:0]), .b(out_12[5:0]), .mul(_3A));
  Mul #(.Bits(6)) mul_3 (.a(A_A[5:0]), .b(A_A[5:0]), .mul(_4A));
  Mul #(.Bits(6)) mul_4 (.a(_4A[5:0]), .b(out_12[5:0]), .mul(_5A));
  Mul #(.Bits(6)) mul_5 (.a(A_A[5:0]), .b(_4A[5:0]), .mul(_6A));
  Mul #(.Bits(6)) mul_6 (.a(_4A[5:0]), .b(_3A[5:0]), .mul(_7A));
  Comparator #(.Bits(8)) comparator_1 (
    .a(out_12), .b(out_13), .gt(greater_flag), .eq(comparator_1_eq), .lt(lesser_flag));
  or or_1 (or_1_out, resethold, opcode11111);
  Add #(.Bits(8)) add_1 (.a(out_12), .b(out_13), .c_i(1'b0), .s(A_plus_B));  // open: c_o
  Sub #(.Bits(8)) sub_1 (.a(out_12), .b(out_13), .c_i(1'b0), .s(A_B_t_t));  // open: c_o
  Mul #(.Bits(4)) mul_7 (.a(out_12[3:0]), .b(out_13[3:0]), .mul(A_B_t));
  Div #(.Bits(8)) div_1 (.a(out_12), .b(out_13), .q(A_B_t_t_t), .r(A_B));
  and and_1 (and_1_out, prime, opcode11101hold);
  and and_2 (and_2_out, or_1_out, Id);
  or or_2 (or_2_out, comparator_1_eq, and_1_out);
  Multiplexer #(.Bits(8)) multiplexer_2 (
    .sel(ResetCounter2Jumphold), .in_0({8{1'b0}}), .in_1(Oprandjump), .out(multiplexer_2_out));
  Multiplexer #(.Selector_Bits(3), .Bits(6)) multiplexer_3 (
    .sel(out_13[2:0]), .in_0(6'b000001), .in_1(out_12[5:0]), .in_2(A_A[5:0]), .in_3(_3A[5:0]),
    .in_4(_4A[5:0]), .in_5(_5A[5:0]), .in_6(_6A[5:0]), .in_7(_7A[5:0]), .out(A_B2));
  and and_3 (and_3_out, starthold, ~futurehold);  // And
  and and_4 (Id2, and_2_out, ~futurehold);  // And
  D_FF #(.Bits(8)) d_ff_1 (.D(multiplexer_2_out), .C(clk), .Q(d_ff_1_q));  // open: nQ
  or or_3 (or_3_out, reset, ResetCounter2Jump);
  Neg #(.Bits(8)) neg_1 (.in(out_12), .out(neg_1_out));
  Multiplexer multiplexer_4 (.sel(opcode11101hold), .in_0(or_2_out), .in_1(prime), .out(equal_flag));
  Counter #(.Bits(8)) counter_1 (.en(and_3_out), .C(clk), .clr(or_3_out), .out(Counter2));  // open: ovf
  or or_4 (Id, progLoad, starthold);
  Multiplexer #(.Bits(8)) multiplexer_5 (.sel(ResetCounter2Jump), .in_0(d_ff_1_q), .in_1(out_11), .out(Oprandjump));
  Sub #(.Bits(8)) sub_2 (.a(neg_1_out), .b(8'h1), .c_i(1'b0), .s(sub_2_s));  // open: c_o
  and and_5 (Bitand[0], out_12[0], out_13[0]);
  and and_6 (Bitand[1], out_12[1], out_13[1]);
  and and_7 (Bitand[2], out_12[2], out_13[2]);
  and and_8 (Bitand[3], out_12[3], out_13[3]);
  and and_9 (Bitand[4], out_12[4], out_13[4]);
  and and_10 (Bitand[5], out_12[5], out_13[5]);
  and and_11 (Bitand[6], out_12[6], out_13[6]);
  and and_12 (Bitand[7], out_12[7], out_13[7]);
  D_FF #(.Bits(8)) d_ff_2 (.D(Oprandjump), .C(clk), .Q(d_ff_2_q));  // open: nQ
  not not_1 (clear, reset);
  Add #(.Bits(8)) add_2 (.a(Counter2), .b(d_ff_2_q), .c_i(1'b0), .s(add_2_s));  // open: c_o
  Multiplexer #(.Selector_Bits(5), .Bits(8)) multiplexer_6 (
    .sel(out_10), .in_0(out_12), .in_1(out_11), .in_2(out_12), .in_3(out_13), .in_4(out_12), .in_5(out_12),
    .in_6(out_14), .in_7(out_12), .in_8(out_12), .in_9(pRAMtoacc), .in_10(out_19), .in_11(out_12),
    .in_12(out_12), .in_13(out_12), .in_14(out_12), .in_15(out_12), .in_16(out_12), .in_17(A_plus_B),
    .in_18(A_B_t_t), .in_19(A_B_t), .in_20(A_B_t_t_t), .in_21(A_B), .in_22({2'b00, A_B2}), .in_23(out_12),
    .in_24(sub_2_s), .in_25(Bitand), .in_26(Bitor), .in_27(Bitxor), .in_28(shift), .in_29(out_12),
    .in_30(out_12), .in_31(out_12), .out(SelaccA));
  Multiplexer #(.Selector_Bits(5)) multiplexer_7 (
    .sel(out_10), .in_0(1'b1), .in_1(1'b1), .in_2(1'b1), .in_3(1'b1), .in_4(1'b1), .in_5(1'b1), .in_6(1'b1),
    .in_7(1'b1), .in_8(1'b1), .in_9(1'b1), .in_10(1'b1), .in_11(1'b1), .in_12(1'b1), .in_13(1'b1),
    .in_14(1'b1), .in_15(1'b1), .in_16(1'b1), .in_17(1'b1), .in_18(1'b1), .in_19(1'b1), .in_20(1'b1),
    .in_21(1'b1), .in_22(1'b1), .in_23(1'b1), .in_24(1'b1), .in_25(1'b1), .in_26(1'b1), .in_27(1'b1),
    .in_28(1'b1), .in_29(1'b1), .in_30(1'b1), .in_31(1'b0), .out(opcode11111));
  Counter #(.Bits(8)) counter_2 (.en(Id), .C(clk), .clr(reset), .out(Counter));  // open: ovf
  Multiplexer #(.Bits(8)) multiplexer_8 (.sel(starthold), .in_0(Counter), .in_1(add_2_s), .out(multiplexer_8_out));
  Sub #(.Bits(8)) sub_3 (.a(a_t), .b(b_t), .c_i(1'b0), .s(sub_3_s));  // open: c_o
  not not_2 (not_2_out, Eq);
  RAMDualAccess #(.AddrBits(8), .Bits(13)) pRAM (
    .str(progLoad), .C(clk), .ld(Id2), .A1(multiplexer_8_out), .Din1(progIN), .A2(out_11),
    .D1({pRAM_d1_2, pRAM_d1}), .D2({opcode2, pRAMtoacc}));
  or or_5 (Bitor[0], out_12[0], out_13[0]);
  or or_6 (Bitor[1], out_12[1], out_13[1]);
  or or_7 (Bitor[2], out_12[2], out_13[2]);
  or or_8 (Bitor[3], out_12[3], out_13[3]);
  or or_9 (Bitor[4], out_12[4], out_13[4]);
  or or_10 (Bitor[5], out_12[5], out_13[5]);
  or or_11 (Bitor[6], out_12[6], out_13[6]);
  or or_12 (Bitor[7], out_12[7], out_13[7]);
  Multiplexer #(.Bits(8)) multiplexer_9 (.sel(A3NEW), .in_0(out_24), .in_1(sub_3_s), .out(multiplexer_9_out));
  Register #(.Bits(8)) RegA (.D(multiplexer_9_out), .C(clk), .en(Loada), .Q(a_t));
  Register #(.Bits(8)) RegOut (.D(a_t), .C(clk), .en(A1NEW), .Q(GCDOUTPUT));
  Multiplexer #(.Selector_Bits(2)) multiplexer_10 (
    .sel({Qa, Qb}), .in_0(1'b0), .in_1(not_2_out), .in_2(1'b0), .in_3(1'b0), .out(multiplexer_10_out));
  Decoder #(.Selector_Bits(2)) decoder_1 (.sel({Qa, Qb}), .out_0(A0NEW), .out_1(A1NEW), .out_2(A2NEW), .out_3(A3NEW));
  Multiplexer #(.Selector_Bits(5), .Bits(8)) multiplexer_11 (
    .sel(out_10), .in_0(out_13), .in_1(out_13), .in_2(out_11), .in_3(out_13), .in_4(out_12), .in_5(out_13),
    .in_6(out_13), .in_7(out_13), .in_8(out_13), .in_9(out_13), .in_10(out_13), .in_11(out_13),
    .in_12(out_13), .in_13(out_13), .in_14(out_13), .in_15(out_13), .in_16(out_13), .in_17(out_13),
    .in_18(out_13), .in_19(out_13), .in_20(out_13), .in_21(out_13), .in_22(out_13), .in_23(out_13),
    .in_24(out_13), .in_25(out_13), .in_26(out_13), .in_27(out_13), .in_28(out_13), .in_29(out_13),
    .in_30(out_13), .in_31(out_13), .out(SelaccB));
  or or_13 (or_13_out, equal_flag, greater_flag);
  not not_3 (busy, busy2);
  and and_13 (and_13_out, multiplexer_10_out, clear);
  Multiplexer #(.Selector_Bits(5)) multiplexer_12 (
    .sel(out_10), .in_0(1'b0), .in_1(1'b0), .in_2(1'b0), .in_3(1'b0), .in_4(1'b0), .in_5(1'b0), .in_6(1'b0),
    .in_7(1'b0), .in_8(1'b0), .in_9(1'b0), .in_10(1'b0), .in_11(1'b0), .in_12(1'b1), .in_13(equal_flag),
    .in_14(greater_flag), .in_15(lesser_flag), .in_16(or_13_out), .in_17(1'b0), .in_18(1'b0), .in_19(1'b0),
    .in_20(1'b0), .in_21(1'b0), .in_22(1'b0), .in_23(1'b0), .in_24(1'b0), .in_25(1'b0), .in_26(1'b0),
    .in_27(1'b0), .in_28(1'b0), .in_29(1'b0), .in_30(1'b0), .in_31(1'b0), .out(ResetCounter2Jump));
  Sub #(.Bits(8)) sub_4 (.a(b_t), .b(a_t), .c_i(1'b0), .s(sub_4_s));  // open: c_o
  Comparator #(.Bits(8)) comparator_2 (.a(a_t), .b(b_t), .gt(Ag), .eq(Eq));  // open: lt
  Multiplexer #(.Bits(8)) multiplexer_13 (.sel(A2NEW), .in_0(out_23), .in_1(sub_4_s), .out(multiplexer_13_out));
  Register #(.Bits(8)) RegB (.D(multiplexer_13_out), .C(clk), .en(Loadb), .Q(b_t));
  D_FF d_ff_3 (.D(and_13_out), .C(clk), .Q(Qa));  // open: nQ
  Multiplexer #(.Bits(8)) multiplexer_14 (.sel(resethold), .in_0(pRAM_d1), .in_1({8{1'b0}}), .out(out_11));
  Multiplexer #(.Bits(5)) multiplexer_15 (.sel(resethold), .in_0(pRAM_d1_2), .in_1({5{1'b0}}), .out(out_10));
  Multiplexer #(.Selector_Bits(5), .Bits(8)) multiplexer_16 (
    .sel(out_10), .in_0(out_14), .in_1(out_14), .in_2(out_14), .in_3(out_14), .in_4(out_14), .in_5(out_12),
    .in_6(out_14), .in_7(M), .in_8(N), .in_9(out_14), .in_10(out_14), .in_11(out_14), .in_12(out_14),
    .in_13(out_14), .in_14(out_14), .in_15(out_14), .in_16(out_14), .in_17(out_14), .in_18(out_14),
    .in_19(out_14), .in_20(out_14), .in_21(out_14), .in_22(out_14), .in_23(out_14), .in_24(out_14),
    .in_25(out_14), .in_26(out_14), .in_27(out_14), .in_28(out_14), .in_29(out_14), .in_30(out_14),
    .in_31(out_14), .out(SelregC));
  xor xor_1 (Bitxor[0], out_12[0], out_13[0]);
  xor xor_2 (Bitxor[1], out_12[1], out_13[1]);
  xor xor_3 (Bitxor[2], out_12[2], out_13[2]);
  xor xor_4 (Bitxor[3], out_12[3], out_13[3]);
  xor xor_5 (Bitxor[4], out_12[4], out_13[4]);
  xor xor_6 (Bitxor[5], out_12[5], out_13[5]);
  xor xor_7 (Bitxor[6], out_12[6], out_13[6]);
  xor xor_8 (Bitxor[7], out_12[7], out_13[7]);
  not not_4 (busy2, A0NEW);
  or or_14 (Loada, A0NEW, A3NEW);
  or or_15 (Loadb, A0NEW, A2NEW);
  not not_5 (not_5_out, Eq);
  and and_14 (and_14_out, Ag, not_5_out);
  Register #(.Bits(8)) accA (.D(SelaccA), .C(~clk), .en(1'b1), .Q(out_12));
  Register #(.Bits(8)) accB (.D(SelaccB), .C(~clk), .en(1'b1), .Q(out_13));
  Register #(.Bits(8)) regC (.D(SelregC), .C(~clk), .en(1'b1), .Q(out_14));
  Multiplexer #(.Selector_Bits(5)) multiplexer_17 (
    .sel(out_10), .in_0(1'b0), .in_1(1'b0), .in_2(1'b0), .in_3(1'b0), .in_4(1'b0), .in_5(1'b0), .in_6(1'b0),
    .in_7(1'b0), .in_8(1'b0), .in_9(1'b0), .in_10(1'b0), .in_11(1'b1), .in_12(1'b0), .in_13(1'b0),
    .in_14(1'b0), .in_15(1'b0), .in_16(1'b0), .in_17(1'b0), .in_18(1'b0), .in_19(1'b0), .in_20(1'b0),
    .in_21(1'b0), .in_22(1'b0), .in_23(1'b0), .in_24(1'b0), .in_25(1'b0), .in_26(1'b0), .in_27(1'b0),
    .in_28(1'b0), .in_29(1'b0), .in_30(1'b0), .in_31(1'b0), .out(rRAMActive));
  Multiplexer #(.Selector_Bits(2)) multiplexer_18 (
    .sel({Qa, Qb}), .in_0(future), .in_1(and_14_out), .in_2(1'b1), .in_3(1'b1), .out(multiplexer_18_out));
  ROM #(.AddrBits(8)) rom_1 (.A(out_12), .sel(1'b1), .D(prime));
  and and_15 (and_15_out, multiplexer_18_out, clear);
  BarrelShifter #(.Bits(8)) barrelshifter_1 (.in(out_12), .shift({1'b0, out_13[2:0]}), .out(shift));
  Counter counter_3 (.en(busy), .C(clk), .clr(future), .out(counter_3_out));  // open: ovf
  D_FF d_ff_4 (.D(and_15_out), .C(clk), .Q(Qb));  // open: nQ
  Multiplexer #(.Bits(8)) multiplexer_19 (.sel(counter_3_out), .in_0(out_20), .in_1(out_21), .out(multiplexer_19_out));
  Multiplexer #(.Bits(8)) multiplexer_20 (.sel(resethold), .in_0(out_12), .in_1({8{1'b0}}), .out(multiplexer_20_out));
  Counter #(.Bits(2)) counter_4 (.en(busy), .C(clk), .clr(future), .out(counter_4_out));  // open: ovf
  Multiplexer #(.Bits(8)) multiplexer_21 (
    .sel(futurehold), .in_0(multiplexer_20_out), .in_1(multiplexer_19_out), .out(multiplexer_21_out));
  or or_16 (or_16_out, result, reset);
  or or_17 (or_17_out, rRAMActive, futurehold, resethold);
  Comparator #(.Bits(2)) comparator_3 (.a(counter_4_out), .b(2'b01), .gt(comparator_3_gt));  // open: eq, lt
  Counter #(.Bits(8)) counter_5 (.en(resulthold), .C(clk), .clr(or_16_out), .out(counter_5_out));  // open: ovf
  Multiplexer #(.Selector_Bits(5)) multiplexer_22 (
    .sel(out_10), .in_0(1'b0), .in_1(1'b0), .in_2(1'b0), .in_3(1'b0), .in_4(1'b0), .in_5(1'b0), .in_6(1'b0),
    .in_7(1'b0), .in_8(1'b0), .in_9(1'b0), .in_10(1'b0), .in_11(1'b0), .in_12(1'b0), .in_13(1'b0),
    .in_14(1'b0), .in_15(1'b0), .in_16(1'b0), .in_17(1'b0), .in_18(1'b0), .in_19(1'b0), .in_20(1'b0),
    .in_21(1'b0), .in_22(1'b0), .in_23(1'b0), .in_24(1'b0), .in_25(1'b0), .in_26(1'b0), .in_27(1'b0),
    .in_28(1'b0), .in_29(1'b0), .in_30(1'b1), .in_31(1'b0), .out(future));
  Multiplexer #(.Selector_Bits(5)) multiplexer_23 (
    .sel(out_10), .in_0(1'b0), .in_1(1'b0), .in_2(1'b0), .in_3(1'b0), .in_4(1'b0), .in_5(1'b0), .in_6(1'b0),
    .in_7(1'b0), .in_8(1'b0), .in_9(1'b0), .in_10(1'b0), .in_11(1'b0), .in_12(1'b0), .in_13(1'b0),
    .in_14(1'b0), .in_15(1'b0), .in_16(1'b0), .in_17(1'b0), .in_18(1'b0), .in_19(1'b0), .in_20(1'b0),
    .in_21(1'b0), .in_22(1'b0), .in_23(1'b1), .in_24(1'b0), .in_25(1'b0), .in_26(1'b0), .in_27(1'b0),
    .in_28(1'b0), .in_29(1'b0), .in_30(1'b0), .in_31(1'b0), .out(multiplexer_23_out));
  and and_16 (and_16_out, busy, or_17_out);
  and and_17 (and_17_out, ~reset, starthold);  // And
  or or_18 (or_18_out, multiplexer_23_out, reset);
  and and_18 (and_18_out, ~reset, resulthold);  // And
  and and_19 (and_19_out, resethold, ~start);  // And
  and and_20 (and_20_out, ~reset, ResetCounter2Jumphold);  // And
  and and_21 (and_21_out, ~comparator_3_gt, futurehold);  // And
  or or_19 (or_19_out, Id, future, resulthold);
  or or_20 (or_20_out, and_18_out, result);
  or or_21 (or_21_out, reset, and_19_out);
  or or_22 (or_22_out, and_17_out, start);
  and and_22 (and_22_out, ~or_18_out, opcode11101hold);  // And
  Multiplexer #(.Bits(8)) multiplexer_24 (
    .sel(future), .in_0(counter_5_out), .in_1({4'b0000, out_11[3:0]}), .out(multiplexer_24_out));
  or or_23 (or_23_out, and_22_out, opcode11101);
  or or_24 (or_24_out, and_20_out, ResetCounter2Jump);
  or or_25 (or_25_out, and_21_out, future);
  not not_6 (not_6_out, clk);
  D_FF d_ff_5 (.D(or_20_out), .C(clk), .Q(resulthold));  // open: nQ
  D_FF d_ff_6 (.D(or_21_out), .C(clk), .Q(resethold));  // open: nQ
  D_FF d_ff_7 (.D(or_22_out), .C(clk), .Q(starthold));  // open: nQ
  D_FF d_ff_8 (.D(or_25_out), .C(clk), .Q(futurehold));  // open: nQ
  RAMDualAccess #(.AddrBits(8), .Bits(8)) rRAM (
    .str(and_16_out), .C(not_6_out), .ld(or_19_out), .A1(addressrRAM), .Din1(multiplexer_21_out),
    .A2(multiplexer_24_out), .D1(out_19), .D2(out_22));
  Comparator #(.Bits(8)) comparator_4 (.a(multiplexer_24_out), .b(8'hf), .gt(done));  // open: eq, lt
  Counter #(.Bits(8)) counter_6 (.en(resethold), .C(clk), .clr(reset), .out(counter_6_out));  // open: ovf
  D_FF d_ff_9 (.D(or_23_out), .C(clk), .Q(opcode11101hold));  // open: nQ
  D_FF d_ff_10 (.D(or_24_out), .C(~clk), .Q(ResetCounter2Jumphold));  // open: nQ
  D_FF d_ff_11 (.D(starthold), .C(~clk), .Q(d_ff_11_q));  // open: nQ
  Multiplexer #(.Bits(8)) multiplexer_25 (.sel(resethold), .in_0(out_11), .in_1(counter_6_out), .out(_1A));
  Multiplexer #(.Bits(8)) multiplexer_26 (.sel(resulthold), .in_0({8{1'b0}}), .in_1(out_22), .out(\output ));
  Seven_Seg_Hex seven_seg_hex_1 (.d(\output [7:4]), .dp(1'b0));
  Multiplexer multiplexer_27 (.sel(reset), .in_0(d_ff_11_q), .in_1(1'b0), .out(valid));
  Seven_Seg_Hex seven_seg_hex_2 (.d(\output [3:0]), .dp(1'b0));
  Register #(.Bits(8)) u_M (.D(out_19), .C(~clk), .en(future), .Q(out_23));
  Multiplexer #(.Bits(8)) multiplexer_28 (
    .sel(future), .in_0(_1A), .in_1({4'b0000, out_11[7:4]}), .out(multiplexer_28_out));
  D_FF #(.Bits(8)) d_ff_12 (.D(out_19), .C(clk), .Q(rRAMtoaccNew));  // open: nQ
  Counter #(.Bits(8)) counter_7 (.en(busy), .C(clk), .clr(future), .out(counter_7_out));  // open: ovf
  Add #(.Bits(8)) add_3 (.a(8'he), .b(counter_7_out), .c_i(1'b0), .s(add_3_s));  // open: c_o
  Register #(.Bits(8)) u_N (.D(out_22), .C(~clk), .en(future), .Q(out_24));
  Multiplexer #(.Bits(8)) multiplexer_29 (
    .sel(futurehold), .in_0(multiplexer_28_out), .in_1(add_3_s), .out(addressrRAM));
  Mul #(.Bits(8)) mul_8 (.a(out_24), .b(out_23), .mul(mul_8_mul));
  Div #(.Bits(16)) div_2 (.a(mul_8_mul), .b({{8{1'b0}}, GCDOUTPUT}), .q({out_20, out_21}));  // open: r

  assign out_15 = out_10;
  assign out_16 = out_11;

  // Other names for the same wires on the sheet: F[7:0] = out_21; E[7:0] = out_20; START_t = future;
  //   GCD[7:0] = out_22; LoadOut = A1NEW; B[7:0] = out_23; Mhold[7:0] = out_23; A[7:0] = out_24; Nhold[7:0] = out_24;
  //   opcode[4:0] = out_10; n_t[3:0] = out_11[3:0]; oprand[7:0] = out_11; m_t[3:0] = out_11[7:4];
  //   out[7:0] = GCDOUTPUT; A0 = out_12[0]; A4bit[5:0] = out_12[5:0]; outputA[7:0] = out_12; A1 = out_12[1];
  //   A2 = out_12[2]; A3 = out_12[3]; A4 = out_12[4]; A5 = out_12[5]; A6 = out_12[6]; A7 = out_12[7]; B0 = out_13[0];
  //   outputB[7:0] = out_13; B1 = out_13[1]; B2 = out_13[2]; B3 = out_13[3]; B4 = out_13[4]; B5 = out_13[5];
  //   B6 = out_13[6]; B7 = out_13[7]; outputC[7:0] = out_14; rRAMtoacc[7:0] = out_19; Sela = A3NEW; Selb = A2NEW

  // Notes on the sheet:
  //   ชื่อกลุ่ม: 3สหายจภ.
  //   สมาชิก
  //   1.6733095021 ธนภูมิ สายวงศ์อินทร์(ผู้ออกแบบและพัฒนาวงจรหลักคนที่ 1)
  //   2.6733296821 เอ็มเมอริก สุภาสุทธิ์(ผู้ออกแบบและพัฒนาวงจรหลักคนที่ 2)
  //   3.6733295121 เอกรัตน์ สุวรรณรัตน์
  //   contents of rom_1 (hex, n*v repeats v):
  //   0,0,1,1,0,1,0,1,0,0,0,1,0,1,0,0,0,1,0,1,0,0,0,1,5*0,1,0,1,5*0
  //   ,1,0,0,0,1,0,1,0,0,1,6*0,1,5*0,1,0,1,5*0,1,0,0,0,1,0,1,5*0,1,0,0,0
  //   ,1,5*0,1,7*0,1,0,0,0,1,0,1,0,0,0,1,0,1,0,0,0,1,13*0,1,0,0,0,1
  //   ,5*0,1,0,1,9*0,1,0,1,5*0,1,5*0,1,0,0,0,1,5*0,1,5*0,1,0,1,9*0,1
  //   ,0,1,0,0,0,1,0,1,11*0,1,11*0,1,0,0,0,1,0,1,0,0,0,1,5*0,1,0,1,9*0,1
endmodule

/* Test case 07_P06T01:
M	N	progIN	reset	progLoad	start	result	clk	valid	done	output
0	0	0	0	0	0	0	0	x	x	x
0	0	0	0	0	0	0	1	x	x	x
0	0	0	1	0	0	0	0	x	x	x
0	0	0	1	0	0	0	1	0	0	x
0	0	0	0	0	0	0	0	0	0	x
0	0	0	0	0	0	0	1	0	0	x
0	0	0	0	0	0	0	0	0	0	x
0	0	0	0	0	0	0	1	0	0	x
0	0	0	0	0	0	0	0	0	0	x
0	0	0	0	0	0	0	1	0	0	x
0	0	0	0	0	0	0	0	0	0	x
0	0	0	0	0	0	0	1	0	0	x
0	0	0	0	0	0	0	0	0	0	x
0	0	0	0	0	0	0	1	0	0	x
0	0	0	0	0	0	0	0	0	0	x
0	0	0	0	0	0	0	1	0	0	x
0	0	0	0	0	0	0	0	0	0	x
0	0	0	0	0	0	0	1	0	0	x
0	0	0	0	0	0	0	0	0	0	x
0	0	0	0	0	0	0	1	0	0	x
0	0	0	0	0	0	0	0	0	0	x
0	0	0	0	0	0	0	1	0	0	x
0	0	0	0	0	0	0	0	0	0	x
0	0	0	0	0	0	0	1	0	0	x
0	0	0	0	0	0	0	0	0	0	x
0	0	0	0	0	0	0	1	0	0	x
0	0	0	0	0	0	0	0	0	0	x
0	0	0	0	0	0	0	1	0	0	x
0	0	0	0	0	0	0	0	0	0	x
0	0	0	0	0	0	0	1	0	0	x
0	0	0	0	0	0	0	0	0	0	x
0	0	0	0	0	0	0	1	0	0	x
0	0	0	0	0	0	0	0	0	0	x
0	0	0	0	0	0	0	1	0	0	x
0	0	0	0	0	0	0	0	0	0	x
0	0	0	0	0	0	0	1	0	0	x
0	0	0	0	0	0	0	0	0	0	x
0	0	0	0	0	0	0	1	0	0	x
0	0	0	0	0	0	0	0	0	0	x
0	0	0	0	0	0	0	1	0	0	x
0	0	0	0	0	0	0	0	0	0	x
0	0	0	0	0	0	0	1	0	0	x
0	0	1792	0	1	0	0	0	0	0	x
0	0	1792	0	1	0	0	1	0	0	x
0	0	1536	0	1	0	0	0	0	0	x
0	0	1536	0	1	0	0	1	0	0	x
0	0	2817	0	1	0	0	0	0	0	x
0	0	2817	0	1	0	0	1	0	0	x
0	0	2048	0	1	0	0	0	0	0	x
0	0	2048	0	1	0	0	1	0	0	x
0	0	1536	0	1	0	0	0	0	0	x
0	0	1536	0	1	0	0	1	0	0	x
0	0	2818	0	1	0	0	0	0	0	x
0	0	2818	0	1	0	0	1	0	0	x
0	0	1024	0	1	0	0	0	0	0	x
0	0	1024	0	1	0	0	1	0	0	x
0	0	2561	0	1	0	0	0	0	0	x
0	0	2561	0	1	0	0	1	0	0	x
0	0	4864	0	1	0	0	0	0	0	x
0	0	4864	0	1	0	0	1	0	0	x
0	0	2819	0	1	0	0	0	0	0	x
0	0	2819	0	1	0	0	1	0	0	x
0	0	2561	0	1	0	0	0	0	0	x
0	0	2561	0	1	0	0	1	0	0	x
0	0	5120	0	1	0	0	0	0	0	x
0	0	5120	0	1	0	0	1	0	0	x
0	0	2820	0	1	0	0	0	0	0	x
0	0	2820	0	1	0	0	1	0	0	x
0	0	7936	0	1	0	0	0	0	0	x
0	0	7936	0	1	0	0	1	0	0	x
15	7	0	0	0	1	0	0	0	0	x
15	7	0	0	0	1	0	1	0	0	x
15	7	0	0	0	0	0	0	x	0	x
15	7	0	0	0	0	0	1	x	0	x
15	7	0	0	0	0	0	0	x	0	x
15	7	0	0	0	0	0	1	x	0	x
15	7	0	0	0	0	0	0	x	0	x
15	7	0	0	0	0	0	1	x	0	x
15	7	0	0	0	0	0	0	x	0	x
15	7	0	0	0	0	0	1	x	0	x
15	7	0	0	0	0	0	0	x	0	x
15	7	0	0	0	0	0	1	x	0	x
15	7	0	0	0	0	0	0	x	0	x
15	7	0	0	0	0	0	1	x	0	x
15	7	0	0	0	0	0	0	x	0	x
15	7	0	0	0	0	0	1	x	0	x
15	7	0	0	0	0	0	0	x	0	x
15	7	0	0	0	0	0	1	x	0	x
15	7	0	0	0	0	0	0	x	0	x
15	7	0	0	0	0	0	1	x	0	x
15	7	0	0	0	0	0	0	x	0	x
15	7	0	0	0	0	0	1	x	0	x
15	7	0	0	0	0	0	0	x	0	x
15	7	0	0	0	0	0	1	x	0	x
15	7	0	0	0	0	0	0	x	0	x
15	7	0	0	0	0	0	1	x	0	x
15	7	0	0	0	0	0	0	x	0	x
15	7	0	0	0	0	0	1	x	0	x
15	7	0	0	0	0	0	0	x	0	x
15	7	0	0	0	0	0	1	x	0	x
15	7	0	0	0	0	0	0	x	0	x
15	7	0	0	0	0	0	1	x	0	x
15	7	0	0	0	0	0	0	x	0	x
15	7	0	0	0	0	0	1	x	0	x
15	7	0	0	0	0	0	0	x	0	x
15	7	0	0	0	0	0	1	x	0	x
15	7	0	0	0	0	0	0	x	0	x
15	7	0	0	0	0	0	1	x	0	x
15	7	0	0	0	0	0	0	x	0	x
15	7	0	0	0	0	0	1	x	0	x
15	7	0	0	0	0	0	0	x	0	x
0	0	0	0	0	0	0	1	x	0	x
0	0	0	0	0	0	0	0	x	0	x
0	0	0	0	0	0	0	1	x	0	x
0	0	0	0	0	0	0	0	x	0	x
0	0	0	0	0	0	0	1	x	0	x
0	0	0	0	0	0	0	0	x	0	x
0	0	0	0	0	0	0	1	x	0	x
0	0	0	0	0	0	0	0	x	0	x
0	0	0	0	0	0	0	1	x	0	x
0	0	0	0	0	0	0	0	x	0	x
0	0	0	0	0	0	0	1	x	0	x
0	0	0	0	0	0	0	0	x	0	x
0	0	0	0	0	0	0	1	1	0	x
0	0	0	0	0	0	1	0	1	0	0
0	0	0	0	0	0	1	1	1	0	0
0	0	0	0	0	0	0	0	1	0	0
0	0	0	0	0	0	0	1	1	0	15
0	0	0	0	0	0	0	0	1	0	15
0	0	0	0	0	0	0	1	1	0	7
0	0	0	0	0	0	0	0	1	0	7
0	0	0	0	0	0	0	1	1	0	105
0	0	0	0	0	0	0	0	1	0	105
0	0	0	0	0	0	0	1	1	0	2
0	0	0	0	0	0	0	0	1	0	2
0	0	0	0	0	0	0	1	1	0	0
0	0	0	0	0	0	0	0	1	0	0
0	0	0	0	0	0	0	1	1	0	0
0	0	0	0	0	0	0	0	1	0	0
0	0	0	0	0	0	0	1	1	0	0
0	0	0	0	0	0	0	0	1	0	0
0	0	0	0	0	0	0	1	1	0	0
0	0	0	0	0	0	0	0	1	0	0
0	0	0	0	0	0	0	1	1	0	0
0	0	0	0	0	0	0	0	1	0	0
0	0	0	0	0	0	0	1	1	0	0
0	0	0	0	0	0	0	0	1	0	0
0	0	0	0	0	0	0	1	1	0	0
0	0	0	0	0	0	0	0	1	0	0
0	0	0	0	0	0	0	1	1	0	0
0	0	0	0	0	0	0	0	1	0	0
0	0	0	0	0	0	0	1	1	0	0
0	0	0	0	0	0	0	0	1	0	0
0	0	0	0	0	0	0	1	1	0	0
0	0	0	0	0	0	0	0	1	0	0
0	0	0	0	0	0	0	1	1	0	0
0	0	0	0	0	0	0	0	1	0	0
0	0	0	0	0	0	0	1	1	1	x
0	0	0	0	0	0	0	0	1	1	x
0	0	0	0	0	0	0	1	1	1	x
0	0	0	0	0	0	0	0	1	1	x
*/

/* Test case 01_P01T2:
M N progIN reset progLoad start result clk valid done output
0 0 0 0 0 0 0 0 x x x
0 0 0 0 0 0 0 1 x x x
0 0 0 1 0 0 0 0 x x x
0 0 0 1 0 0 0 1 0 0 0
0 0 0 0 0 0 0 0 0 0 0
0 0 0 0 0 0 0 1 0 0 0
0 0 0 0 0 0 0 0 0 0 0
0 0 0 0 0 0 0 1 0 0 0
0 0 0 0 0 0 0 0 0 0 0
0 0 0 0 0 0 0 1 0 0 0
0 0 0 0 0 0 0 0 0 0 0
0 0 0 0 0 0 0 1 0 0 0
0 0 0 0 0 0 0 0 0 0 0
0 0 0 0 0 0 0 1 0 0 0
0 0 0 0 0 0 0 0 0 0 0
0 0 0 0 0 0 0 1 0 0 0
0 0 0 0 0 0 0 0 0 0 0
0 0 0 0 0 0 0 1 0 0 0
0 0 0 0 0 0 0 0 0 0 0
0 0 0 0 0 0 0 1 0 0 0
0 0 0 0 0 0 0 0 0 0 0
0 0 0 0 0 0 0 1 0 0 0
0 0 0 0 0 0 0 0 0 0 0
0 0 0 0 0 0 0 1 0 0 0
0 0 0 0 0 0 0 0 0 0 0
0 0 0 0 0 0 0 1 0 0 0
0 0 0 0 0 0 0 0 0 0 0
0 0 0 0 0 0 0 1 0 0 0
0 0 0 0 0 0 0 0 0 0 0
0 0 0 0 0 0 0 1 0 0 0
0 0 0 0 0 0 0 0 0 0 0
0 0 0 0 0 0 0 1 0 0 0
0 0 0 0 0 0 0 0 0 0 0
0 0 0 0 0 0 0 1 0 0 0
0 0 0 0 0 0 0 0 0 0 0
0 0 0 0 0 0 0 1 0 0 0
0 0 0 0 0 0 0 0 0 0 0
0 0 0 0 0 0 0 1 0 0 0
0 0 0 0 0 0 0 0 0 0 0
0 0 0 0 0 0 0 1 0 0 0
0 0 0 0 0 0 0 0 0 0 0
0 0 0 0 0 0 0 1 0 0 0
0 0 271 0 1 0 0 0 0 0 0
0 0 271 0 1 0 0 1 0 0 0
0 0 565 0 1 0 0 0 0 0 0
0 0 565 0 1 0 0 1 0 0 0
0 0 4352 0 1 0 0 0 0 0 0
0 0 4352 0 1 0 0 1 0 0 0
0 0 2819 0 1 0 0 0 0 0 0
0 0 2819 0 1 0 0 1 0 0 0
0 0 7936 0 1 0 0 0 0 0 0
0 0 7936 0 1 0 0 1 0 0 0
0 0 0 0 0 1 0 0 0 0 0
0 0 0 0 0 1 0 1 0 0 0
0 0 0 0 0 0 0 0 x 0 0
0 0 0 0 0 0 0 1 x 0 0
0 0 0 0 0 0 0 0 x 0 0
0 0 0 0 0 0 0 1 x 0 0
0 0 0 0 0 0 0 0 x 0 0
0 0 0 0 0 0 0 1 x 0 0
0 0 0 0 0 0 0 0 x 0 0
0 0 0 0 0 0 0 1 x 0 0
0 0 0 0 0 0 0 0 x 0 0
0 0 0 0 0 0 0 1 x 0 0
0 0 0 0 0 0 0 0 x 0 0
0 0 0 0 0 0 0 1 x 0 0
0 0 0 0 0 0 0 0 x 0 0
0 0 0 0 0 0 0 1 x 0 0
0 0 0 0 0 0 0 0 x 0 0
0 0 0 0 0 0 0 1 x 0 0
0 0 0 0 0 0 0 0 x 0 0
0 0 0 0 0 0 0 1 x 0 0
0 0 0 0 0 0 0 0 x 0 0
0 0 0 0 0 0 0 1 x 0 0
0 0 0 0 0 0 0 0 x 0 0
0 0 0 0 0 0 0 1 x 0 0
0 0 0 0 0 0 0 0 x 0 0
0 0 0 0 0 0 0 1 x 0 0
0 0 0 0 0 0 0 0 x 0 0
0 0 0 0 0 0 0 1 x 0 0
0 0 0 0 0 0 0 0 x 0 0
0 0 0 0 0 0 0 1 x 0 0
0 0 0 0 0 0 0 0 x 0 0
0 0 0 0 0 0 0 1 x 0 0
0 0 0 0 0 0 0 0 x 0 0
0 0 0 0 0 0 0 1 x 0 0
0 0 0 0 0 0 0 0 x 0 0
0 0 0 0 0 0 0 1 x 0 0
0 0 0 0 0 0 0 0 x 0 0
0 0 0 0 0 0 0 1 x 0 0
0 0 0 0 0 0 0 0 x 0 0
0 0 0 0 0 0 0 1 x 0 0
0 0 0 0 0 0 0 0 x 0 0
0 0 0 0 0 0 0 1 x 0 0
0 0 0 0 0 0 0 0 x 0 0
0 0 0 0 0 0 0 1 x 0 0
0 0 0 0 0 0 0 0 x 0 0
0 0 0 0 0 0 0 1 x 0 0
0 0 0 0 0 0 0 0 x 0 0
0 0 0 0 0 0 0 1 x 0 0
0 0 0 0 0 0 0 0 x 0 0
0 0 0 0 0 0 0 1 x 0 0
0 0 0 0 0 0 0 0 x 0 0
0 0 0 0 0 0 0 1 x 0 0
0 0 0 0 0 0 0 0 x 0 0
0 0 0 0 0 0 0 1 1 0 0
0 0 0 0 0 0 1 0 1 0 0
0 0 0 0 0 0 1 1 1 0 0
0 0 0 0 0 0 0 0 1 0 0
0 0 0 0 0 0 0 1 1 0 0
0 0 0 0 0 0 0 0 1 0 0
0 0 0 0 0 0 0 1 1 0 0
0 0 0 0 0 0 0 0 1 0 0
0 0 0 0 0 0 0 1 1 0 68
0 0 0 0 0 0 0 0 1 0 68
0 0 0 0 0 0 0 1 1 0 0
0 0 0 0 0 0 0 0 1 0 0
0 0 0 0 0 0 0 1 1 0 0
0 0 0 0 0 0 0 0 1 0 0
0 0 0 0 0 0 0 1 1 0 0
0 0 0 0 0 0 0 0 1 0 0
0 0 0 0 0 0 0 1 1 0 0
0 0 0 0 0 0 0 0 1 0 0
0 0 0 0 0 0 0 1 1 0 0
0 0 0 0 0 0 0 0 1 0 0
0 0 0 0 0 0 0 1 1 0 0
0 0 0 0 0 0 0 0 1 0 0
0 0 0 0 0 0 0 1 1 0 0
0 0 0 0 0 0 0 0 1 0 0
0 0 0 0 0 0 0 1 1 0 0
0 0 0 0 0 0 0 0 1 0 0
0 0 0 0 0 0 0 1 1 0 0
0 0 0 0 0 0 0 0 1 0 0
0 0 0 0 0 0 0 1 1 0 0
0 0 0 0 0 0 0 0 1 0 0
0 0 0 0 0 0 0 1 1 0 0
0 0 0 0 0 0 0 0 1 0 0
0 0 0 0 0 0 0 1 1 0 0
0 0 0 0 0 0 0 0 1 0 0
0 0 0 0 0 0 0 1 1 1 0
0 0 0 0 0 0 0 0 1 1 0
0 0 0 0 0 0 0 1 1 1 0
0 0 0 0 0 0 0 0 1 1 0
*/

/* Test case 02_P01T3:
M N progIN reset progLoad start result clk valid done output
0 0 0 0 0 0 0 0 x x x
0 0 0 0 0 0 0 1 x x x
0 0 0 1 0 0 0 0 x x x
0 0 0 1 0 0 0 1 0 0 0
0 0 0 0 0 0 0 0 0 0 0
0 0 0 0 0 0 0 1 0 0 0
0 0 0 0 0 0 0 0 0 0 0
0 0 0 0 0 0 0 1 0 0 0
0 0 0 0 0 0 0 0 0 0 0
0 0 0 0 0 0 0 1 0 0 0
0 0 0 0 0 0 0 0 0 0 0
0 0 0 0 0 0 0 1 0 0 0
0 0 0 0 0 0 0 0 0 0 0
0 0 0 0 0 0 0 1 0 0 0
0 0 0 0 0 0 0 0 0 0 0
0 0 0 0 0 0 0 1 0 0 0
0 0 0 0 0 0 0 0 0 0 0
0 0 0 0 0 0 0 1 0 0 0
0 0 0 0 0 0 0 0 0 0 0
0 0 0 0 0 0 0 1 0 0 0
0 0 0 0 0 0 0 0 0 0 0
0 0 0 0 0 0 0 1 0 0 0
0 0 0 0 0 0 0 0 0 0 0
0 0 0 0 0 0 0 1 0 0 0
0 0 0 0 0 0 0 0 0 0 0
0 0 0 0 0 0 0 1 0 0 0
0 0 0 0 0 0 0 0 0 0 0
0 0 0 0 0 0 0 1 0 0 0
0 0 0 0 0 0 0 0 0 0 0
0 0 0 0 0 0 0 1 0 0 0
0 0 0 0 0 0 0 0 0 0 0
0 0 0 0 0 0 0 1 0 0 0
0 0 0 0 0 0 0 0 0 0 0
0 0 0 0 0 0 0 1 0 0 0
0 0 0 0 0 0 0 0 0 0 0
0 0 0 0 0 0 0 1 0 0 0
0 0 0 0 0 0 0 0 0 0 0
0 0 0 0 0 0 0 1 0 0 0
0 0 0 0 0 0 0 0 0 0 0
0 0 0 0 0 0 0 1 0 0 0
0 0 0 0 0 0 0 0 0 0 0
0 0 0 0 0 0 0 1 0 0 0
0 0 271 0 1 0 0 0 0 0 0
0 0 271 0 1 0 0 1 0 0 0
0 0 565 0 1 0 0 0 0 0 0
0 0 565 0 1 0 0 1 0 0 0
0 0 4352 0 1 0 0 0 0 0 0
0 0 4352 0 1 0 0 1 0 0 0
0 0 2819 0 1 0 0 0 0 0 0
0 0 2819 0 1 0 0 1 0 0 0
0 0 7936 0 1 0 0 0 0 0 0
0 0 7936 0 1 0 0 1 0 0 0
0 0 0 0 0 1 0 0 0 0 0
0 0 0 0 0 1 0 1 0 0 0
0 0 0 0 0 0 0 0 x 0 0
0 0 0 0 0 0 0 1 x 0 0
0 0 0 0 0 0 0 0 x 0 0
0 0 0 0 0 0 0 1 x 0 0
0 0 0 0 0 0 0 0 x 0 0
0 0 0 0 0 0 0 1 x 0 0
0 0 0 0 0 0 0 0 x 0 0
0 0 0 0 0 0 0 1 x 0 0
0 0 0 0 0 0 0 0 x 0 0
0 0 0 0 0 0 0 1 x 0 0
0 0 0 0 0 0 0 0 x 0 0
0 0 0 0 0 0 0 1 x 0 0
0 0 0 0 0 0 0 0 x 0 0
0 0 0 0 0 0 0 1 x 0 0
0 0 0 0 0 0 0 0 x 0 0
0 0 0 0 0 0 0 1 x 0 0
0 0 0 0 0 0 0 0 x 0 0
0 0 0 0 0 0 0 1 x 0 0
0 0 0 0 0 0 0 0 x 0 0
0 0 0 0 0 0 0 1 x 0 0
0 0 0 0 0 0 0 0 x 0 0
0 0 0 0 0 0 0 1 x 0 0
0 0 0 0 0 0 0 0 x 0 0
0 0 0 0 0 0 0 1 x 0 0
0 0 0 0 0 0 0 0 x 0 0
0 0 0 0 0 0 0 1 x 0 0
0 0 0 0 0 0 0 0 x 0 0
0 0 0 0 0 0 0 1 x 0 0
0 0 0 0 0 0 0 0 x 0 0
0 0 0 0 0 0 0 1 x 0 0
0 0 0 0 0 0 0 0 x 0 0
0 0 0 0 0 0 0 1 x 0 0
0 0 0 0 0 0 0 0 x 0 0
0 0 0 0 0 0 0 1 x 0 0
0 0 0 0 0 0 0 0 x 0 0
0 0 0 0 0 0 0 1 x 0 0
0 0 0 0 0 0 0 0 x 0 0
0 0 0 0 0 0 0 1 x 0 0
0 0 0 0 0 0 0 0 x 0 0
0 0 0 0 0 0 0 1 x 0 0
0 0 0 0 0 0 0 0 x 0 0
0 0 0 0 0 0 0 1 x 0 0
0 0 0 0 0 0 0 0 x 0 0
0 0 0 0 0 0 0 1 x 0 0
0 0 0 0 0 0 0 0 x 0 0
0 0 0 0 0 0 0 1 x 0 0
0 0 0 0 0 0 0 0 x 0 0
0 0 0 0 0 0 0 1 x 0 0
0 0 0 0 0 0 0 0 x 0 0
0 0 0 0 0 0 0 1 x 0 0
0 0 0 0 0 0 0 0 x 0 0
0 0 0 0 0 0 0 1 1 0 0
0 0 0 0 0 0 1 0 1 0 0
0 0 0 0 0 0 1 1 1 0 0
0 0 0 0 0 0 0 0 1 0 0
0 0 0 0 0 0 0 1 1 0 0
0 0 0 0 0 0 0 0 1 0 0
0 0 0 0 0 0 0 1 1 0 0
0 0 0 0 0 0 0 0 1 0 0
0 0 0 0 0 0 0 1 1 0 68
0 0 0 0 0 0 0 0 1 0 68
0 0 0 0 0 0 0 1 1 0 0
0 0 0 0 0 0 0 0 1 0 0
0 0 0 0 0 0 0 1 1 0 0
0 0 0 0 0 0 0 0 1 0 0
0 0 0 0 0 0 0 1 1 0 0
0 0 0 0 0 0 0 0 1 0 0
0 0 0 0 0 0 0 1 1 0 0
0 0 0 0 0 0 0 0 1 0 0
0 0 0 0 0 0 0 1 1 0 0
0 0 0 0 0 0 0 0 1 0 0
0 0 0 0 0 0 0 1 1 0 0
0 0 0 0 0 0 0 0 1 0 0
0 0 0 0 0 0 0 1 1 0 0
0 0 0 0 0 0 0 0 1 0 0
0 0 0 0 0 0 0 1 1 0 0
0 0 0 0 0 0 0 0 1 0 0
0 0 0 0 0 0 0 1 1 0 0
0 0 0 0 0 0 0 0 1 0 0
0 0 0 0 0 0 0 1 1 0 0
0 0 0 0 0 0 0 0 1 0 0
0 0 0 0 0 0 0 1 1 0 0
0 0 0 0 0 0 0 0 1 0 0
0 0 0 0 0 0 0 1 1 0 0
0 0 0 0 0 0 0 0 1 0 0
0 0 0 0 0 0 0 1 1 1 0
0 0 0 0 0 0 0 0 1 1 0
0 0 0 0 0 0 0 1 1 1 0
0 0 0 0 0 0 0 0 1 1 0
0 0 0 0 0 0 0 1 1 1 0
0 0 0 0 0 0 1 0 1 X 0
0 0 0 0 0 0 1 1 1 X 0
0 0 0 0 0 0 0 0 1 0 0
0 0 0 0 0 0 0 1 1 0 0
0 0 0 0 0 0 0 0 1 0 0
0 0 0 0 0 0 0 1 1 0 0
0 0 0 0 0 0 0 0 1 0 0
0 0 0 0 0 0 0 1 1 0 68
0 0 0 0 0 0 0 0 1 0 68
0 0 0 0 0 0 0 1 1 0 0
0 0 0 0 0 0 0 0 1 0 0
0 0 0 0 0 0 0 1 1 0 0
0 0 0 0 0 0 0 0 1 0 0
0 0 0 0 0 0 0 1 1 0 0
0 0 0 0 0 0 0 0 1 0 0
0 0 0 0 0 0 0 1 1 0 0
0 0 0 0 0 0 0 0 1 0 0
0 0 0 0 0 0 0 1 1 0 0
0 0 0 0 0 0 0 0 1 0 0
0 0 0 0 0 0 0 1 1 0 0
0 0 0 0 0 0 0 0 1 0 0
0 0 0 0 0 0 0 1 1 0 0
0 0 0 0 0 0 0 0 1 0 0
0 0 0 0 0 0 0 1 1 0 0
0 0 0 0 0 0 0 0 1 0 0
0 0 0 0 0 0 0 1 1 0 0
0 0 0 0 0 0 0 0 1 0 0
0 0 0 0 0 0 0 1 1 0 0
0 0 0 0 0 0 0 0 1 0 0
0 0 0 0 0 0 0 1 1 0 0
0 0 0 0 0 0 0 0 1 0 0
0 0 0 0 0 0 0 1 1 0 0
0 0 0 0 0 0 0 0 1 0 0
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*/

/* Test case 08_P06T02:
M	N	progIN	reset	progLoad	start	result	clk	valid	done	output
0	0	0	0	0	0	0	0	x	x	x
0	0	0	0	0	0	0	1	x	x	x
0	0	0	1	0	0	0	0	x	x	x
0	0	0	1	0	0	0	1	0	0	x
0	0	0	0	0	0	0	0	0	0	x
0	0	0	0	0	0	0	1	0	0	x
0	0	0	0	0	0	0	0	0	0	x
0	0	0	0	0	0	0	1	0	0	x
0	0	0	0	0	0	0	0	0	0	x
0	0	0	0	0	0	0	1	0	0	x
0	0	0	0	0	0	0	0	0	0	x
0	0	0	0	0	0	0	1	0	0	x
0	0	0	0	0	0	0	0	0	0	x
0	0	0	0	0	0	0	1	0	0	x
0	0	0	0	0	0	0	0	0	0	x
0	0	0	0	0	0	0	1	0	0	x
0	0	0	0	0	0	0	0	0	0	x
0	0	0	0	0	0	0	1	0	0	x
0	0	0	0	0	0	0	0	0	0	x
0	0	0	0	0	0	0	1	0	0	x
0	0	0	0	0	0	0	0	0	0	x
0	0	0	0	0	0	0	1	0	0	x
0	0	0	0	0	0	0	0	0	0	x
0	0	0	0	0	0	0	1	0	0	x
0	0	0	0	0	0	0	0	0	0	x
0	0	0	0	0	0	0	1	0	0	x
0	0	0	0	0	0	0	0	0	0	x
0	0	0	0	0	0	0	1	0	0	x
0	0	0	0	0	0	0	0	0	0	x
0	0	0	0	0	0	0	1	0	0	x
0	0	0	0	0	0	0	0	0	0	x
0	0	0	0	0	0	0	1	0	0	x
0	0	0	0	0	0	0	0	0	0	x
0	0	0	0	0	0	0	1	0	0	x
0	0	0	0	0	0	0	0	0	0	x
0	0	0	0	0	0	0	1	0	0	x
0	0	0	0	0	0	0	0	0	0	x
0	0	0	0	0	0	0	1	0	0	x
0	0	0	0	0	0	0	0	0	0	x
0	0	0	0	0	0	0	1	0	0	x
0	0	0	0	0	0	0	0	0	0	x
0	0	0	0	0	0	0	1	0	0	x
0	0	1792	0	1	0	0	0	0	0	x
0	0	1792	0	1	0	0	1	0	0	x
0	0	1536	0	1	0	0	0	0	0	x
0	0	1536	0	1	0	0	1	0	0	x
0	0	2817	0	1	0	0	0	0	0	x
0	0	2817	0	1	0	0	1	0	0	x
0	0	2048	0	1	0	0	0	0	0	x
0	0	2048	0	1	0	0	1	0	0	x
0	0	1536	0	1	0	0	0	0	0	x
0	0	1536	0	1	0	0	1	0	0	x
0	0	2818	0	1	0	0	0	0	0	x
0	0	2818	0	1	0	0	1	0	0	x
0	0	1024	0	1	0	0	0	0	0	x
0	0	1024	0	1	0	0	1	0	0	x
0	0	2561	0	1	0	0	0	0	0	x
0	0	2561	0	1	0	0	1	0	0	x
0	0	4864	0	1	0	0	0	0	0	x
0	0	4864	0	1	0	0	1	0	0	x
0	0	2819	0	1	0	0	0	0	0	x
0	0	2819	0	1	0	0	1	0	0	x
0	0	2561	0	1	0	0	0	0	0	x
0	0	2561	0	1	0	0	1	0	0	x
0	0	5120	0	1	0	0	0	0	0	x
0	0	5120	0	1	0	0	1	0	0	x
0	0	2820	0	1	0	0	0	0	0	x
0	0	2820	0	1	0	0	1	0	0	x
0	0	7936	0	1	0	0	0	0	0	x
0	0	7936	0	1	0	0	1	0	0	x
15	7	0	0	0	1	0	0	0	0	x
15	7	0	0	0	1	0	1	0	0	x
15	7	0	0	0	0	0	0	x	0	x
15	7	0	0	0	0	0	1	x	0	x
15	7	0	0	0	0	0	0	x	0	x
15	7	0	0	0	0	0	1	x	0	x
15	7	0	0	0	0	0	0	x	0	x
15	7	0	0	0	0	0	1	x	0	x
15	7	0	0	0	0	0	0	x	0	x
15	7	0	0	0	0	0	1	x	0	x
15	7	0	0	0	0	0	0	x	0	x
15	7	0	0	0	0	0	1	x	0	x
15	7	0	0	0	0	0	0	x	0	x
15	7	0	0	0	0	0	1	x	0	x
15	7	0	0	0	0	0	0	x	0	x
15	7	0	0	0	0	0	1	x	0	x
15	7	0	0	0	0	0	0	x	0	x
15	7	0	0	0	0	0	1	x	0	x
15	7	0	0	0	0	0	0	x	0	x
15	7	0	0	0	0	0	1	x	0	x
15	7	0	0	0	0	0	0	x	0	x
15	7	0	0	0	0	0	1	x	0	x
15	7	0	0	0	0	0	0	x	0	x
15	7	0	0	0	0	0	1	x	0	x
15	7	0	0	0	0	0	0	x	0	x
15	7	0	0	0	0	0	1	x	0	x
15	7	0	0	0	0	0	0	x	0	x
15	7	0	0	0	0	0	1	x	0	x
15	7	0	0	0	0	0	0	x	0	x
15	7	0	0	0	0	0	1	x	0	x
15	7	0	0	0	0	0	0	x	0	x
15	7	0	0	0	0	0	1	x	0	x
15	7	0	0	0	0	0	0	x	0	x
15	7	0	0	0	0	0	1	x	0	x
15	7	0	0	0	0	0	0	x	0	x
15	7	0	0	0	0	0	1	x	0	x
15	7	0	0	0	0	0	0	x	0	x
15	7	0	0	0	0	0	1	x	0	x
15	7	0	0	0	0	0	0	x	0	x
15	7	0	0	0	0	0	1	x	0	x
15	7	0	0	0	0	0	0	x	0	x
0	0	0	0	0	0	0	1	x	0	x
0	0	0	0	0	0	0	0	x	0	x
0	0	0	0	0	0	0	1	x	0	x
0	0	0	0	0	0	0	0	x	0	x
0	0	0	0	0	0	0	1	x	0	x
0	0	0	0	0	0	0	0	x	0	x
0	0	0	0	0	0	0	1	x	0	x
0	0	0	0	0	0	0	0	x	0	x
0	0	0	0	0	0	0	1	x	0	x
0	0	0	0	0	0	0	0	x	0	x
0	0	0	0	0	0	0	1	x	0	x
0	0	0	0	0	0	0	0	x	0	x
0	0	0	0	0	0	0	1	1	0	x
0	0	0	0	0	0	1	0	1	0	0
0	0	0	0	0	0	1	1	1	0	0
0	0	0	0	0	0	0	0	1	0	0
0	0	0	0	0	0	0	1	1	0	15
0	0	0	0	0	0	0	0	1	0	15
0	0	0	0	0	0	0	1	1	0	7
0	0	0	0	0	0	0	0	1	0	7
0	0	0	0	0	0	0	1	1	0	105
0	0	0	0	0	0	0	0	1	0	105
0	0	0	0	0	0	0	1	1	0	2
0	0	0	0	0	0	0	0	1	0	2
0	0	0	0	0	0	0	1	1	0	0
0	0	0	0	0	0	0	0	1	0	0
0	0	0	0	0	0	0	1	1	0	0
0	0	0	0	0	0	0	0	1	0	0
0	0	0	0	0	0	0	1	1	0	0
0	0	0	0	0	0	0	0	1	0	0
0	0	0	0	0	0	0	1	1	0	0
0	0	0	0	0	0	0	0	1	0	0
0	0	0	0	0	0	0	1	1	0	0
0	0	0	0	0	0	0	0	1	0	0
0	0	0	0	0	0	0	1	1	0	0
0	0	0	0	0	0	0	0	1	0	0
0	0	0	0	0	0	0	1	1	0	0
0	0	0	0	0	0	0	0	1	0	0
0	0	0	0	0	0	0	1	1	0	0
0	0	0	0	0	0	0	0	1	0	0
0	0	0	0	0	0	0	1	1	0	0
0	0	0	0	0	0	0	0	1	0	0
0	0	0	0	0	0	0	1	1	0	0
0	0	0	0	0	0	0	0	1	0	0
0	0	0	0	0	0	0	1	1	0	0
0	0	0	0	0	0	0	0	1	0	0
0	0	0	0	0	0	0	1	1	1	x
0	0	0	0	0	0	0	0	1	1	x
0	0	0	0	0	0	0	1	1	1	x
0	0	0	0	0	0	0	0	1	1	x
0	0	0	0	0	0	0	1	1	1	x
0	0	0	1	0	0	0	0	x	x	x
0	0	0	1	0	0	0	1	0	0	x
0	0	0	0	0	0	0	0	0	0	x
0	0	0	0	0	0	0	1	0	0	x
0	0	0	0	0	0	0	0	0	0	x
0	0	0	0	0	0	0	1	0	0	x
0	0	0	0	0	0	0	0	0	0	x
0	0	0	0	0	0	0	1	0	0	x
0	0	0	0	0	0	0	0	0	0	x
0	0	0	0	0	0	0	1	0	0	x
0	0	0	0	0	0	0	0	0	0	x
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*/

/* Test case 03_P02T2:
M N progIN reset progLoad start result clk valid done output
0 0 0 0 0 0 0 0 x x x
0 0 0 0 0 0 0 1 x x x
0 0 0 1 0 0 0 0 x x x
0 0 0 1 0 0 0 1 0 0 0
0 0 0 0 0 0 0 0 0 0 0
0 0 0 0 0 0 0 1 0 0 0
0 0 0 0 0 0 0 0 0 0 0
0 0 0 0 0 0 0 1 0 0 0
0 0 0 0 0 0 0 0 0 0 0
0 0 0 0 0 0 0 1 0 0 0
0 0 0 0 0 0 0 0 0 0 0
0 0 0 0 0 0 0 1 0 0 0
0 0 0 0 0 0 0 0 0 0 0
0 0 0 0 0 0 0 1 0 0 0
0 0 0 0 0 0 0 0 0 0 0
0 0 0 0 0 0 0 1 0 0 0
0 0 0 0 0 0 0 0 0 0 0
0 0 0 0 0 0 0 1 0 0 0
0 0 0 0 0 0 0 0 0 0 0
0 0 0 0 0 0 0 1 0 0 0
0 0 0 0 0 0 0 0 0 0 0
0 0 0 0 0 0 0 1 0 0 0
0 0 0 0 0 0 0 0 0 0 0
0 0 0 0 0 0 0 1 0 0 0
0 0 0 0 0 0 0 0 0 0 0
0 0 0 0 0 0 0 1 0 0 0
0 0 0 0 0 0 0 0 0 0 0
0 0 0 0 0 0 0 1 0 0 0
0 0 0 0 0 0 0 0 0 0 0
0 0 0 0 0 0 0 1 0 0 0
0 0 0 0 0 0 0 0 0 0 0
0 0 0 0 0 0 0 1 0 0 0
0 0 0 0 0 0 0 0 0 0 0
0 0 0 0 0 0 0 1 0 0 0
0 0 0 0 0 0 0 0 0 0 0
0 0 0 0 0 0 0 1 0 0 0
0 0 0 0 0 0 0 0 0 0 0
0 0 0 0 0 0 0 1 0 0 0
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*/

/* Test case Comment 19:
M N progIN reset progLoad start result clk valid done output
0 0 0 0 0 0 0 0 x x x
0 0 0 0 0 0 0 1 x x x
0 0 0 1 0 0 0 0 x x x
0 0 0 1 0 0 0 1 0 0 0
0 0 0 0 0 0 0 0 0 0 0
0 0 0 0 0 0 0 1 0 0 0
0 0 0 0 0 0 0 0 0 0 0
0 0 0 0 0 0 0 1 0 0 0
0 0 0 0 0 0 0 0 0 0 0
0 0 0 0 0 0 0 1 0 0 0
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*/

/* Test case Jump:
M N progIN reset progLoad start result clk valid done output
0	0	0	0	0	0	0	0	x	x	x
0	0	0	0	0	0	0	1	x	x	x
0	0	0	1	0	0	0	0	x	x	x
0	0	0	1	0	0	0	1	0	0	0
0	0	0	0	0	0	0	0	0	0	0
0	0	0	0	0	0	0	1	0	0	0
0	0	0	0	0	0	0	0	0	0	0
0	0	0	0	0	0	0	1	0	0	0
0	0	0	0	0	0	0	0	0	0	0
0	0	0	0	0	0	0	1	0	0	0
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*/

/* Test case 09_P06T3:
M	N	progIN	reset	progLoad	start	result	clk	valid	done	output
0	0	0	0	0	0	0	0	x	x	x
0	0	0	0	0	0	0	1	x	x	x
0	0	0	1	0	0	0	0	x	x	x
0	0	0	1	0	0	0	1	0	0	x
0	0	0	0	0	0	0	0	0	0	x
0	0	0	0	0	0	0	1	0	0	x
0	0	0	0	0	0	0	0	0	0	x
0	0	0	0	0	0	0	1	0	0	x
0	0	0	0	0	0	0	0	0	0	x
0	0	0	0	0	0	0	1	0	0	x
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*/

/* Test case 11_P06T5:
M	N	progIN	reset	progLoad	start	result	clk	valid	done	output
0	0	0	0	0	0	0	0	x	x	x
0	0	0	0	0	0	0	1	x	x	x
0	0	0	1	0	0	0	0	x	x	x
0	0	0	1	0	0	0	1	0	0	x
0	0	0	0	0	0	0	0	0	0	x
0	0	0	0	0	0	0	1	0	0	x
0	0	0	0	0	0	0	0	0	0	x
0	0	0	0	0	0	0	1	0	0	x
0	0	0	0	0	0	0	0	0	0	x
0	0	0	0	0	0	0	1	0	0	x
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*/

/* Test case Triple Jump:
M N progIN reset progLoad start result clk valid done output
0 0 0 0 0 0 0 0 x x x
0 0 0 0 0 0 0 1 x x x
0 0 0 1 0 0 0 0 x x x
0 0 0 1 0 0 0 1 0 0 0
0 0 0 0 0 0 0 0 0 0 0
0 0 0 0 0 0 0 1 0 0 0
0 0 0 0 0 0 0 0 0 0 0
0 0 0 0 0 0 0 1 0 0 0
0 0 0 0 0 0 0 0 0 0 0
0 0 0 0 0 0 0 1 0 0 0
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*/

/* Test case 10_P06T4:
M	N	progIN	reset	progLoad	start	result	clk	valid	done	output
0	0	0	0	0	0	0	0	x	x	x
0	0	0	0	0	0	0	1	x	x	x
0	0	0	1	0	0	0	0	x	x	x
0	0	0	1	0	0	0	1	0	0	x
0	0	0	0	0	0	0	0	0	0	x
0	0	0	0	0	0	0	1	0	0	x
0	0	0	0	0	0	0	0	0	0	x
0	0	0	0	0	0	0	1	0	0	x
0	0	0	0	0	0	0	0	0	0	x
0	0	0	0	0	0	0	1	0	0	x
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*/

/* Test case 12_P06T6:
M	N	progIN	reset	progLoad	start	result	clk	valid	done	output
0	0	0	0	0	0	0	0	x	x	x
0	0	0	0	0	0	0	1	x	x	x
0	0	0	1	0	0	0	0	x	x	x
0	0	0	1	0	0	0	1	0	0	x
0	0	0	0	0	0	0	0	0	0	x
0	0	0	0	0	0	0	1	0	0	x
0	0	0	0	0	0	0	0	0	0	x
0	0	0	0	0	0	0	1	0	0	x
0	0	0	0	0	0	0	0	0	0	x
0	0	0	0	0	0	0	1	0	0	x
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*/

/* Test case pRAMLoadTest:
M N progIN reset progLoad start result clk valid done output
0 0 0 0 0 0 0 0 x x x
0 0 0 0 0 0 0 1 x x x
0 0 0 1 0 0 0 0 x x x
0 0 0 1 0 0 0 1 0 0 0
0 0 0 0 0 0 0 0 0 0 0
0 0 0 0 0 0 0 1 0 0 0
0 0 0 0 0 0 0 0 0 0 0
0 0 0 0 0 0 0 1 0 0 0
0 0 0 0 0 0 0 0 0 0 0
0 0 0 0 0 0 0 1 0 0 0
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*/

/* Test case Prime:
M N progIN reset progLoad start result clk valid done output
0 0 0 0 0 0 0 0 x x x
0 0 0 0 0 0 0 1 x x x
0 0 0 1 0 0 0 0 x x x
0 0 0 1 0 0 0 1 0 0 0
0 0 0 0 0 0 0 0 0 0 0
0 0 0 0 0 0 0 1 0 0 0
0 0 0 0 0 0 0 0 0 0 0
0 0 0 0 0 0 0 1 0 0 0
0 0 0 0 0 0 0 0 0 0 0
0 0 0 0 0 0 0 1 0 0 0
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*/

/* Test case 13_P06T7:
M	N	progIN	reset	progLoad	start	result	clk	valid	done	output
0	0	0	0	0	0	0	0	x	x	x
0	0	0	0	0	0	0	1	x	x	x
0	0	0	1	0	0	0	0	x	x	x
0	0	0	1	0	0	0	1	0	0	x
0	0	0	0	0	0	0	0	0	0	x
0	0	0	0	0	0	0	1	0	0	x
0	0	0	0	0	0	0	0	0	0	x
0	0	0	0	0	0	0	1	0	0	x
0	0	0	0	0	0	0	0	0	0	x
0	0	0	0	0	0	0	1	0	0	x
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*/

/* Test case 14_P06T8:
M	N	progIN	reset	progLoad	start	result	clk	valid	done	output
0	0	0	0	0	0	0	0	x	x	x
0	0	0	0	0	0	0	1	x	x	x
0	0	0	1	0	0	0	0	x	x	x
0	0	0	1	0	0	0	1	0	0	x
0	0	0	0	0	0	0	0	0	0	x
0	0	0	0	0	0	0	1	0	0	x
0	0	0	0	0	0	0	0	0	0	x
0	0	0	0	0	0	0	1	0	0	x
0	0	0	0	0	0	0	0	0	0	x
0	0	0	0	0	0	0	1	0	0	x
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*/
